// Logisim project PROCESSADOR.circ as structural Verilog: 3 circuits, main circuit main
// OP
module main (
  input  [1:0] in_1,
  input  [4:0] RD,
  input  [4:0] RT,
  input  [4:0] RS
);

  wire button_1_out;
  wire [31:0] banco_de_registradores_1_rs_out, banco_de_registradores_1_rt_out, \ula_1_saída ;

  Button button_1 (.out(button_1_out));
  Banco_de_Registradores banco_de_registradores_1 (
    .INPUT_VALUE(\ula_1_saída ), .RT_OUT(banco_de_registradores_1_rt_out),
    .RS_OUT(banco_de_registradores_1_rs_out), .RD(RD), .CLK(button_1_out), .RS(RS), .RT(RT));
  ULA ula_1 (
    .RT(banco_de_registradores_1_rt_out), .RS(banco_de_registradores_1_rs_out), .\SAÍDA (\ula_1_saída ),
    .OP(in_1));
endmodule

// BR
module Banco_de_Registradores (
  input  [31:0] INPUT_VALUE,
  input  [4:0] RT,
  input  [4:0] RD,
  input  [4:0] RS,
  input  CLK,
  output [31:0] RT_OUT,
  output [31:0] RS_OUT
);

  wire _1, _2, _3, _4, _5, _6, _7, _8, _9, _10, _11, _12, _13, _14, _15, _16, _17, _18, _19, _20, _21, _22,
       _23, _24, _25, _26, _27, _28, _29, _30, _31, and_1_out, and_2_out, and_3_out, and_4_out, and_5_out,
       and_6_out, and_7_out, and_8_out, and_9_out, and_10_out, and_11_out, and_12_out, and_13_out,
       and_14_out, and_15_out, and_16_out, and_17_out, and_18_out, and_19_out, and_20_out, and_21_out,
       and_22_out, and_23_out, and_24_out, and_25_out, and_26_out, and_27_out, and_28_out, and_29_out,
       and_30_out, and_31_out;
  wire [31:0] S0, S1, S2, S3, S4, S5, S6, S7, S8, S9, S10, S11, S12, S13, S14, S15, S16, S17, S18, S19, S20,
       S21, S22, S23, S24, S25, S26, S27, S28, S29, S30, S31, S230;

  Demultiplexer #(.select(5), .enable("false")) demultiplexer_1 (
    .out1(_1), .out2(_2), .out3(_3), .out4(_4), .out5(_5), .out6(_6), .out7(_7), .out8(_8), .out9(_9),
    .out10(_10), .out11(_11), .out12(_12), .out13(_13), .out14(_14), .out15(_15), .out16(_16), .out17(_17),
    .out18(_18), .out19(_19), .out20(_20), .out21(_21), .out22(_22), .out23(_23), .out24(_24), .out25(_25),
    .out26(_26), .out27(_27), .out28(_28), .out29(_29), .out30(_30), .out31(_31), .in(1'b1), .sel(RD));  // open: out0
  Register #(.width(32)) R0 (.Q(S0));  // open: D, en, clk, clr
  Register #(.width(32)) R8 (.D(INPUT_VALUE), .Q(S8), .clk(and_1_out));  // open: en, clr
  and and_1 (and_1_out, _8, CLK);
  Register #(.width(32)) R16 (.D(INPUT_VALUE), .Q(S16), .clk(and_2_out));  // open: en, clr
  and and_2 (and_2_out, _16, CLK);
  Register #(.width(32)) R24 (.D(INPUT_VALUE), .Q(S24), .clk(and_3_out));  // open: en, clr
  and and_3 (and_3_out, _24, CLK);
  and and_4 (and_4_out, _1, CLK);
  and and_5 (and_5_out, _9, CLK);
  and and_6 (and_6_out, _17, CLK);
  and and_7 (and_7_out, _25, CLK);
  Register #(.width(32)) R1 (.D(INPUT_VALUE), .Q(S1), .clk(and_4_out));  // open: en, clr
  and and_8 (and_8_out, _2, CLK);
  Register #(.width(32)) R9 (.D(INPUT_VALUE), .Q(S9), .clk(and_5_out));  // open: en, clr
  and and_9 (and_9_out, _10, CLK);
  Register #(.width(32)) R17 (.D(INPUT_VALUE), .Q(S17), .clk(and_6_out));  // open: en, clr
  and and_10 (and_10_out, _18, CLK);
  Register #(.width(32)) R25 (.D(INPUT_VALUE), .Q(S25), .clk(and_7_out));  // open: en, clr
  and and_11 (and_11_out, _26, CLK);
  Register #(.width(32)) R2 (.D(INPUT_VALUE), .Q(S2), .clk(and_8_out));  // open: en, clr
  Register #(.width(32)) R10 (.D(INPUT_VALUE), .Q(S10), .clk(and_9_out));  // open: en, clr
  Register #(.width(32)) R18 (.D(INPUT_VALUE), .Q(S18), .clk(and_10_out));  // open: en, clr
  Register #(.width(32)) R26 (.D(INPUT_VALUE), .Q(S26), .clk(and_11_out));  // open: en, clr
  Register #(.width(32)) R3 (.D(INPUT_VALUE), .Q(S3), .clk(and_12_out));  // open: en, clr
  and and_12 (and_12_out, _3, CLK);
  Register #(.width(32)) R11 (.D(INPUT_VALUE), .Q(S11), .clk(and_13_out));  // open: en, clr
  and and_13 (and_13_out, _11, CLK);
  Register #(.width(32)) R19 (.D(INPUT_VALUE), .Q(S19), .clk(and_14_out));  // open: en, clr
  and and_14 (and_14_out, _19, CLK);
  Register #(.width(32)) R27 (.D(INPUT_VALUE), .Q(S27), .clk(and_15_out));  // open: en, clr
  and and_15 (and_15_out, _27, CLK);
  Register #(.width(32)) R4 (.D(INPUT_VALUE), .Q(S4), .clk(and_16_out));  // open: en, clr
  and and_16 (and_16_out, _4, CLK);
  Register #(.width(32)) R12 (.D(INPUT_VALUE), .Q(S12), .clk(and_17_out));  // open: en, clr
  and and_17 (and_17_out, _12, CLK);
  Register #(.width(32)) R20 (.D(INPUT_VALUE), .Q(S20), .clk(and_18_out));  // open: en, clr
  and and_18 (and_18_out, _20, CLK);
  Register #(.width(32)) R28 (.D(INPUT_VALUE), .Q(S28), .clk(and_19_out));  // open: en, clr
  and and_19 (and_19_out, _28, CLK);
  Register #(.width(32)) R5 (.D(INPUT_VALUE), .Q(S5), .clk(and_20_out));  // open: en, clr
  and and_20 (and_20_out, _5, CLK);
  Register #(.width(32)) R13 (.D(INPUT_VALUE), .Q(S13), .clk(and_21_out));  // open: en, clr
  and and_21 (and_21_out, _13, CLK);
  Register #(.width(32)) R21 (.D(INPUT_VALUE), .Q(S21), .clk(and_22_out));  // open: en, clr
  and and_22 (and_22_out, _21, CLK);
  Register #(.width(32)) R29 (.D(INPUT_VALUE), .Q(S29), .clk(and_23_out));  // open: en, clr
  and and_23 (and_23_out, _29, CLK);
  Register #(.width(32)) R6 (.D(INPUT_VALUE), .Q(S6), .clk(and_24_out));  // open: en, clr
  and and_24 (and_24_out, _6, CLK);
  Register #(.width(32)) R14 (.D(INPUT_VALUE), .Q(S14), .clk(and_25_out));  // open: en, clr
  and and_25 (and_25_out, _14, CLK);
  Register #(.width(32)) R22 (.D(INPUT_VALUE), .Q(S22), .clk(and_26_out));  // open: en, clr
  and and_26 (and_26_out, _22, CLK);
  Register #(.width(32)) R30 (.D(INPUT_VALUE), .Q(S230), .clk(and_27_out));  // open: en, clr
  and and_27 (and_27_out, _30, CLK);
  Register #(.width(32)) R7 (.D(INPUT_VALUE), .Q(S7), .clk(and_28_out));  // open: en, clr
  and and_28 (and_28_out, _7, CLK);
  Register #(.width(32)) R15 (.D(INPUT_VALUE), .Q(S15), .clk(and_29_out));  // open: en, clr
  and and_29 (and_29_out, _15, CLK);
  Register #(.width(32)) R23 (.D(INPUT_VALUE), .Q(S23), .clk(and_30_out));  // open: en, clr
  and and_30 (and_30_out, _23, CLK);
  Register #(.width(32)) R31 (.D(INPUT_VALUE), .Q(S31), .clk(and_31_out));  // open: en, clr
  and and_31 (and_31_out, _31, CLK);
  Multiplexer #(.select(5), .width(32), .enable("false")) multiplexer_1 (
    .in0(S0), .in1(S1), .in2(S2), .in3(S3), .in4(S4), .in5(S5), .in6(S6), .in7(S7), .in8(S8), .in9(S9),
    .in10(S10), .in11(S11), .in12(S12), .in13(S13), .in14(S14), .in15(S15), .in16(S16), .in17(S17),
    .in18(S18), .in19(S19), .in20(S20), .in21(S21), .in22(S22), .in23(S23), .in24(S24), .in25(S25),
    .in26(S26), .in27(S27), .in28(S28), .in29(S29), .in30(S30), .in31(S31), .out(RT_OUT), .sel(RT));
  Multiplexer #(.select(5), .width(32), .enable("false")) multiplexer_2 (
    .in0(S0), .in1(S1), .in2(S2), .in3(S3), .in4(S4), .in5(S5), .in6(S6), .in7(S7), .in8(S8), .in9(S9),
    .in10(S10), .in11(S11), .in12(S12), .in13(S13), .in14(S14), .in15(S15), .in16(S16), .in17(S17),
    .in18(S18), .in19(S19), .in20(S20), .in21(S21), .in22(S22), .in23(S23), .in24(S24), .in25(S25),
    .in26(S26), .in27(S27), .in28(S28), .in29(S29), .in30(S30), .in31(S31), .out(RS_OUT), .sel(RS));
endmodule

module ULA (
  input  [31:0] RT,
  input  [31:0] RS,
  input  [1:0] OP,
  output [31:0] \SAÍDA 
);

  wire [31:0] adder_1_out, subtractor_1_out;

  Adder #(.width(32)) adder_1 (.a(RT), .b(RS), .out(adder_1_out));  // open: cin, cout
  Subtractor #(.width(32)) subtractor_1 (.a(RT), .b(RS), .out(subtractor_1_out));  // open: bin, bout
  Multiplexer #(.select(2), .width(32), .enable("false")) multiplexer_1 (
    .in0(adder_1_out), .in1(subtractor_1_out), .out(\SAÍDA ), .sel(OP));  // open: in2, in3
endmodule
